// Logisim project 19101284.circ as structural Verilog: 9 circuits, main circuit main
module main (
  input  in_1,
  input  in_2
);

  wire clock_1_out, not_1_out, not_2_out, not_3_out, not_4_out, oneoftwodecoder_1_y0, oneoftwodecoder_1_y1,
       oneoftwodecoder_1_y2, oneoftwodecoder_1_y3;
  wire [1:0] twobitcounter_1_d;
  wire [15:0] transistor_1_out, transistor_1_out_2, transistor_1_out_3, transistor_1_out_4, transistor_2_out,
       transistor_2_out_2, transistor_2_out_3, transistor_2_out_4, transistor_3_out_2;
  wire [47:0] transistor_3_out;
  wire [63:0] channel_1_l1, channel_1_l2, channel_1_l3, channel_1_l4, transistor_4_out, transistor_5_out,
       transistor_6_out, transistor_7_out, transistor_8_out, transistor_9_out, transistor_10_out,
       transistor_11_out, transistor_12_out, transistor_13_out, transistor_14_out, transistor_15_out,
       transistor_16_out;

  Clock clock_1 (.out(clock_1_out));
  TwoBitCounter twobitcounter_1 (.CLK(clock_1_out), .D(twobitcounter_1_d));
  Hex_Digit_Display #(.decimalPoint("false")) hex_digit_display_1 (.value({2'b00, twobitcounter_1_d}));
  Channel channel_1 (
    .in_1(in_1), .in_2(in_2), .L1(channel_1_l1), .L2(channel_1_l2), .L3(channel_1_l3), .L4(channel_1_l4));
  OneOfTwoDecoder oneoftwodecoder_1 (
    .A(twobitcounter_1_d[0]), .B(twobitcounter_1_d[1]), .Y0(oneoftwodecoder_1_y0), .Y1(oneoftwodecoder_1_y1),
    .Y2(oneoftwodecoder_1_y2), .Y3(oneoftwodecoder_1_y3));
  DotMatrix #(.matrixcols(16), .matrixrows(16)) dotmatrix_1 (
    .col0(transistor_1_out_4), .col1(transistor_1_out_3), .col2(transistor_1_out_2), .col3(transistor_1_out),
    .col4(transistor_2_out_4), .col5(transistor_2_out_3), .col6(transistor_2_out_2), .col7(transistor_2_out),
    .col8(transistor_3_out_2), .col9(transistor_3_out[47:32]), .col10(transistor_3_out[31:16]),
    .col11(transistor_3_out[15:0]), .col12(transistor_6_out[63:48]), .col13(transistor_6_out[47:32]),
    .col14(transistor_6_out[31:16]), .col15(transistor_6_out[15:0]));
  not not_1 (not_1_out, oneoftwodecoder_1_y0);
  not not_2 (not_2_out, oneoftwodecoder_1_y1);
  not not_3 (not_3_out, oneoftwodecoder_1_y2);
  not not_4 (not_4_out, oneoftwodecoder_1_y3);
  Transistor #(.width(64)) transistor_1 (
    .in(channel_1_l1), .out({transistor_1_out_4, transistor_1_out_3, transistor_1_out_2, transistor_1_out}),
    .gate(not_4_out));
  Transistor #(.width(64)) transistor_2 (
    .in(channel_1_l2), .out({transistor_2_out_4, transistor_2_out_3, transistor_2_out_2, transistor_2_out}),
    .gate(not_4_out));
  Transistor #(.width(64)) transistor_3 (
    .in(channel_1_l3), .out({transistor_3_out_2, transistor_3_out}), .gate(not_4_out));
  Transistor #(.width(64)) transistor_4 (.in(channel_1_l1), .out(transistor_4_out), .gate(not_3_out));
  Transistor #(.width(64)) transistor_5 (.in(channel_1_l2), .out(transistor_5_out), .gate(not_3_out));
  Transistor #(.width(64)) transistor_6 (.in(channel_1_l4), .out(transistor_6_out), .gate(not_4_out));
  Transistor #(.width(64)) transistor_7 (.in(channel_1_l1), .out(transistor_7_out), .gate(not_2_out));
  Transistor #(.width(64)) transistor_8 (.in(channel_1_l2), .out(transistor_8_out), .gate(not_2_out));
  Transistor #(.width(64)) transistor_9 (.in(channel_1_l3), .out(transistor_9_out), .gate(not_3_out));
  Transistor #(.width(64)) transistor_10 (.in(channel_1_l4), .out(transistor_10_out), .gate(not_3_out));
  DotMatrix #(.matrixcols(16), .matrixrows(16)) dotmatrix_2 (
    .col0(transistor_4_out[63:48]), .col1(transistor_4_out[47:32]), .col2(transistor_4_out[31:16]),
    .col3(transistor_4_out[15:0]), .col4(transistor_5_out[63:48]), .col5(transistor_5_out[47:32]),
    .col6(transistor_5_out[31:16]), .col7(transistor_5_out[15:0]), .col8(transistor_9_out[63:48]),
    .col9(transistor_9_out[47:32]), .col10(transistor_9_out[31:16]), .col11(transistor_9_out[15:0]),
    .col12(transistor_10_out[63:48]), .col13(transistor_10_out[47:32]), .col14(transistor_10_out[31:16]),
    .col15(transistor_10_out[15:0]));
  Transistor #(.width(64)) transistor_11 (.in(channel_1_l1), .out(transistor_11_out), .gate(not_1_out));
  Transistor #(.width(64)) transistor_12 (.in(channel_1_l3), .out(transistor_12_out), .gate(not_2_out));
  Transistor #(.width(64)) transistor_13 (.in(channel_1_l4), .out(transistor_13_out), .gate(not_2_out));
  Transistor #(.width(64)) transistor_14 (.in(channel_1_l2), .out(transistor_14_out), .gate(not_1_out));
  Transistor #(.width(64)) transistor_15 (.in(channel_1_l3), .out(transistor_15_out), .gate(not_1_out));
  Transistor #(.width(64)) transistor_16 (.in(channel_1_l4), .out(transistor_16_out), .gate(not_1_out));
  DotMatrix #(.matrixcols(16), .matrixrows(16)) dotmatrix_3 (
    .col0(transistor_7_out[63:48]), .col1(transistor_7_out[47:32]), .col2(transistor_7_out[31:16]),
    .col3(transistor_7_out[15:0]), .col4(transistor_8_out[63:48]), .col5(transistor_8_out[47:32]),
    .col6(transistor_8_out[31:16]), .col7(transistor_8_out[15:0]), .col8(transistor_12_out[63:48]),
    .col9(transistor_12_out[47:32]), .col10(transistor_12_out[31:16]), .col11(transistor_12_out[15:0]),
    .col12(transistor_13_out[63:48]), .col13(transistor_13_out[47:32]), .col14(transistor_13_out[31:16]),
    .col15(transistor_13_out[15:0]));
  DotMatrix #(.matrixcols(16), .matrixrows(16)) dotmatrix_4 (
    .col0(transistor_11_out[63:48]), .col1(transistor_11_out[47:32]), .col2(transistor_11_out[31:16]),
    .col3(transistor_11_out[15:0]), .col4(transistor_14_out[63:48]), .col5(transistor_14_out[47:32]),
    .col6(transistor_14_out[31:16]), .col7(transistor_14_out[15:0]), .col8(transistor_15_out[63:48]),
    .col9(transistor_15_out[47:32]), .col10(transistor_15_out[31:16]), .col11(transistor_15_out[15:0]),
    .col12(transistor_16_out[63:48]), .col13(transistor_16_out[47:32]), .col14(transistor_16_out[31:16]),
    .col15(transistor_16_out[15:0]));
endmodule

module HalfAdder (
  input  A,
  input  B,
  output S,
  output C
);

  xor xor_1 (S, A, B);
  and and_1 (C, A, B);
endmodule

module FullAdder (
  input  A,
  input  B,
  input  C_in,
  output S,
  output C_out
);

  wire halfadder_1_c, halfadder_1_s, halfadder_2_c;

  HalfAdder halfadder_1 (.A(A), .B(B), .S(halfadder_1_s), .C(halfadder_1_c));
  HalfAdder halfadder_2 (.A(halfadder_1_s), .B(C_in), .S(S), .C(halfadder_2_c));
  or or_1 (C_out, halfadder_1_c, halfadder_2_c);
endmodule

module MyCounter (
  input  CLK,
  output [7:0] D
);

  wire and_1_out, and_2_out, and_3_out, and_4_out, and_5_out, and_6_out;

  J_K_Flip_Flop j_k_ff_1 (.J(1'b1), .K(1'b1), .clk(CLK), .Q(D[0]));  // open: Qn, preset, reset
  J_K_Flip_Flop j_k_ff_2 (.J(D[0]), .K(D[0]), .clk(CLK), .Q(D[1]));  // open: Qn, preset, reset
  and and_1 (and_1_out, D[0], D[1]);
  J_K_Flip_Flop j_k_ff_3 (.J(and_1_out), .K(and_1_out), .clk(CLK), .Q(D[2]));  // open: Qn, preset, reset
  and and_2 (and_2_out, and_1_out, D[2]);
  J_K_Flip_Flop j_k_ff_4 (.J(and_2_out), .K(and_2_out), .clk(CLK), .Q(D[3]));  // open: Qn, preset, reset
  and and_3 (and_3_out, and_2_out, D[3]);
  J_K_Flip_Flop j_k_ff_5 (.J(and_3_out), .K(and_3_out), .clk(CLK), .Q(D[4]));  // open: Qn, preset, reset
  and and_4 (and_4_out, and_3_out, D[4]);
  J_K_Flip_Flop j_k_ff_6 (.J(and_4_out), .K(and_4_out), .clk(CLK), .Q(D[5]));  // open: Qn, preset, reset
  and and_5 (and_5_out, and_4_out, D[5]);
  J_K_Flip_Flop j_k_ff_7 (.J(and_5_out), .K(and_5_out), .clk(CLK), .Q(D[6]));  // open: Qn, preset, reset
  and and_6 (and_6_out, and_5_out, D[6]);
  J_K_Flip_Flop j_k_ff_8 (.J(and_6_out), .K(and_6_out), .clk(CLK), .Q(D[7]));  // open: Qn, preset, reset
endmodule

module EightBitAdder (
  input  [7:0] A,
  input  [7:0] B,
  output [7:0] S,
  output OVR
);

  wire fulladder_1_c_out, fulladder_2_c_out, fulladder_3_c_out, fulladder_4_c_out, fulladder_5_c_out,
       fulladder_6_c_out, fulladder_7_c_out;

  FullAdder fulladder_1 (.A(A[0]), .B(B[0]), .C_in(1'b0), .S(S[0]), .C_out(fulladder_1_c_out));
  FullAdder fulladder_2 (.A(A[1]), .B(B[1]), .C_in(fulladder_1_c_out), .S(S[1]), .C_out(fulladder_2_c_out));
  FullAdder fulladder_3 (.A(A[2]), .B(B[2]), .C_in(fulladder_2_c_out), .S(S[2]), .C_out(fulladder_3_c_out));
  FullAdder fulladder_4 (.A(A[3]), .B(B[3]), .C_in(fulladder_3_c_out), .S(S[3]), .C_out(fulladder_4_c_out));
  FullAdder fulladder_5 (.A(A[4]), .B(B[4]), .C_in(fulladder_4_c_out), .S(S[4]), .C_out(fulladder_5_c_out));
  FullAdder fulladder_6 (.A(A[5]), .B(B[5]), .C_in(fulladder_5_c_out), .S(S[5]), .C_out(fulladder_6_c_out));
  FullAdder fulladder_7 (.A(A[6]), .B(B[6]), .C_in(fulladder_6_c_out), .S(S[6]), .C_out(fulladder_7_c_out));
  FullAdder fulladder_8 (.A(A[7]), .B(B[7]), .C_in(fulladder_7_c_out), .S(S[7]), .C_out(OVR));
endmodule

module OneOfTwoDecoder (
  input  A,
  input  B,
  output Y0,
  output Y1,
  output Y2,
  output Y3
);

  wire not_1_out, not_2_out;

  not not_1 (not_1_out, A);
  not not_2 (not_2_out, B);
  and and_1 (Y0, not_1_out, not_2_out);
  and and_2 (Y1, A, not_2_out);
  and and_3 (Y2, not_1_out, B);
  and and_4 (Y3, A, B);

  // Notes on the sheet:
  //   OneOfTwoDecoder: Not
endmodule

module TwoBitCounter (
  input  CLK,
  output [1:0] D
);

  J_K_Flip_Flop j_k_ff_1 (.J(1'b1), .K(1'b1), .clk(CLK), .Q(D[0]));  // open: Qn, preset, reset
  J_K_Flip_Flop j_k_ff_2 (.J(D[0]), .K(D[0]), .clk(CLK), .Q(D[1]));  // open: Qn, preset, reset
endmodule

module LedMatrixSumulator (
  input  [7:0] in_1,
  input  [7:0] in_2,
  input  [7:0] in_3,
  input  [7:0] in_4,
  input  [7:0] in_5,
  input  [7:0] in_6,
  input  [7:0] in_7,
  input  [7:0] in_8,
  input  [7:0] in_9,
  input  [7:0] in_10,
  input  [7:0] in_11,
  input  [7:0] in_12,
  input  [7:0] in_13,
  input  [7:0] in_14,
  input  [7:0] in_15,
  input  [7:0] in_16,
  input  [7:0] in_17,
  input  [7:0] in_18,
  input  [7:0] in_19,
  input  [7:0] in_20,
  input  [7:0] in_21,
  input  [7:0] in_22,
  input  [7:0] in_23,
  input  [7:0] in_24,
  input  [7:0] in_25,
  input  [7:0] in_26,
  input  [7:0] in_27,
  input  [7:0] in_28,
  input  [7:0] in_29,
  input  [7:0] in_30,
  input  [7:0] in_31,
  input  [7:0] in_32,
  output [63:0] out_33,
  output [63:0] out_34,
  output [63:0] out_35,
  output [63:0] out_36
);

  DotMatrix #(.matrixcols(16), .matrixrows(16)) dotmatrix_1 (
    .col0({in_1, in_17}), .col1({in_2, in_18}), .col2({in_3, in_19}), .col3({in_4, in_20}),
    .col4({in_5, in_21}), .col5({in_6, in_22}), .col6({in_7, in_23}), .col7({in_8, in_24}),
    .col8({in_9, in_25}), .col9({in_10, in_26}), .col10({in_11, in_27}), .col11({in_12, in_28}),
    .col12({in_13, in_29}), .col13({in_14, in_30}), .col14({in_15, in_31}), .col15({in_16, in_32}));

  assign out_33 = {in_13, in_29, in_14, in_30, in_15, in_31, in_16, in_32};
  assign out_34 = {in_1, in_17, in_2, in_18, in_3, in_19, in_4, in_20};
  assign out_35 = {in_9, in_25, in_10, in_26, in_11, in_27, in_12, in_28};
  assign out_36 = {in_5, in_21, in_6, in_22, in_7, in_23, in_8, in_24};
endmodule

module Channel (
  input  in_1,
  input  in_2,
  output [63:0] L1,
  output [63:0] L2,
  output [63:0] L3,
  output [63:0] L4
);

  wire oneoftwodecoder_1_y0, oneoftwodecoder_1_y1, oneoftwodecoder_1_y2, oneoftwodecoder_1_y3;
  wire [63:0] undriven, undriven_2, undriven_3, undriven_4, undriven_5, undriven_6, undriven_7, undriven_8,
       undriven_9, undriven_10, undriven_11, undriven_12;

  DotMatrix #(.matrixcols(16), .matrixrows(16)) dotmatrix_1 (
    .col0({16{1'b0}}), .col1(16'h10f8), .col2(16'h1004), .col3(16'h7006), .col4(16'h5002), .col5(16'h5382),
    .col6(16'h5392), .col7(16'h5012), .col8(16'h5012), .col9(16'h5392), .col10(16'h5382), .col11(16'h5002),
    .col12(16'h7006), .col13(16'h1004), .col14(16'h10f8), .col15({16{1'b0}}));
  OneOfTwoDecoder oneoftwodecoder_1 (
    .A(in_1), .B(in_2), .Y0(oneoftwodecoder_1_y0), .Y1(oneoftwodecoder_1_y1), .Y2(oneoftwodecoder_1_y2),
    .Y3(oneoftwodecoder_1_y3));
  assign L1 = oneoftwodecoder_1_y2 ? undriven : 64'bz;  // Controlled_Buffer controlled_buffer_1
  assign L1 = oneoftwodecoder_1_y3 ? 64'h10f810047006 : 64'bz;  // Controlled_Buffer controlled_buffer_2
  assign L1 = oneoftwodecoder_1_y0 ? undriven_3 : 64'bz;  // Controlled_Buffer controlled_buffer_3
  assign L1 = oneoftwodecoder_1_y1 ? undriven_2 : 64'bz;  // Controlled_Buffer controlled_buffer_4
  assign L2 = oneoftwodecoder_1_y2 ? undriven_4 : 64'bz;  // Controlled_Buffer controlled_buffer_5
  assign L2 = oneoftwodecoder_1_y3 ? 64'h5002538253925012 : 64'bz;  // Controlled_Buffer controlled_buffer_6
  assign L2 = oneoftwodecoder_1_y0 ? undriven_6 : 64'bz;  // Controlled_Buffer controlled_buffer_7
  assign L2 = oneoftwodecoder_1_y1 ? undriven_5 : 64'bz;  // Controlled_Buffer controlled_buffer_8
  assign L3 = oneoftwodecoder_1_y2 ? undriven_7 : 64'bz;  // Controlled_Buffer controlled_buffer_9
  assign L3 = oneoftwodecoder_1_y3 ? 64'h5012539253825002 : 64'bz;  // Controlled_Buffer controlled_buffer_10
  assign L3 = oneoftwodecoder_1_y0 ? undriven_9 : 64'bz;  // Controlled_Buffer controlled_buffer_11
  assign L3 = oneoftwodecoder_1_y1 ? undriven_8 : 64'bz;  // Controlled_Buffer controlled_buffer_12
  assign L4 = oneoftwodecoder_1_y2 ? undriven_10 : 64'bz;  // Controlled_Buffer controlled_buffer_13
  assign L4 = oneoftwodecoder_1_y3 ? 64'h7006100410f80000 : 64'bz;  // Controlled_Buffer controlled_buffer_14
  assign L4 = oneoftwodecoder_1_y0 ? undriven_12 : 64'bz;  // Controlled_Buffer controlled_buffer_15
  assign L4 = oneoftwodecoder_1_y1 ? undriven_11 : 64'bz;  // Controlled_Buffer controlled_buffer_16
endmodule
